# Fritzing sketch circuit (saved by Fritzing 0.9.2b)
breadboards: 1

parts:
  Part2 = Arduino Pro Mini v13
  LED1 = RGB LED - (4 legs) [package="5 mm [THT]"]
  R1 = Resistor [tolerance=±5% resistance=220 package=THT]
  R2 = Resistor [tolerance=±5% resistance=220 package=THT]
  R3 = Resistor [tolerance=±5% resistance=220 package=THT]
  Part3 = Real Time Clock Module - DS1307 RTC Breakout Board
  Grove1 = Grove OLED 128x96

nets:
  N1: Part2.A4, Part3.SDA, Grove1.SDA
  N2: Part2.A5, Part3.SCL, Grove1.SCL
  GND: Part2.GND, LED1.common_anode, Part3.GND, Grove1.GND
  N3: Part2.D6_PWM, R1.Pin_1
  N4: Part2.D5_PWM, R3.Pin_1
  N5: Part2.D3_PWM, R2.Pin_1
  N6: LED1.red_cathode, R1.Pin_0
  N7: LED1.green_cathode, R3.Pin_0
  N8: LED1.blue_cathode, R2.Pin_0
  5V: Part3.5V, Grove1.VCC
